# Fritzing sketch Drink Lantern (saved by Fritzing 0.8.7b)
circuit board: 5cm x 5cm
breadboards: 1

parts:
  R1 = Resistor [tolerance=±5% resistance=100k package=THT]
  R2 = Resistor [tolerance=±5% resistance=3.3 package=THT]
  Q3 = NPN-Transistor [part_number="Adafruit PID756" package="TO92 [THT]"]
  Q2 = Basic FET N-Channel [part_number="Adafruit PID 355" package="TO220 [THT]"]
  J1 = Screw terminal - 2 pins [package=THT]
  S1 = Pushbutton [package="[THT]"]
  J2 = Screw terminal - 2 pins [package=THT]
  S2 = Pushbutton [package="[THT]"]
  S3 = Pushbutton [package="[THT]"]

nets:
  N1: R1.Pin_0, J1.pin1, S1.Pin_3, S1.Pin_4
  N2: R1.Pin_1, Q3.C, Q2.gate
  N3: R2.Pin_0, Q3.B, Q2.source
  N4: R2.Pin_1, Q3.E, J2.pin2
  N5: Q2.drain, J1.pin2
  N6: S1.Pin_1, S1.Pin_2, J2.pin1
  N7: S2.Pin_1, S2.Pin_2
  N8: S2.Pin_3, S2.Pin_4
  N9: S3.Pin_1, S3.Pin_2
  N10: S3.Pin_3, S3.Pin_4
